# Fritzing sketch Clock_Scheme (saved by Fritzing 1.0.2b)
breadboards: 1

parts:
  Part1 = Arduino Mega 2560 (Rev3)
  RHT1 = Humidity and Temperature Sensor RHT03
  J1 = Piezo Speaker
  Part2 = Real Time Clock Module - DS1307 RTC Breakout Board
  IC1 = SHIFT REGISTER [package=dil16]
  LED1 = 7-SEGMENT-4DIGIT-YOUNGSUN [package=7-segment-4digit-youngsun-longpads]
  Q1 = NPN-Transistor [package="TO92 [THT]"]
  Q2 = NPN-Transistor [package="TO92 [THT]"]
  Q3 = NPN-Transistor [package="TO92 [THT]"]
  Q4 = NPN-Transistor [package="TO92 [THT]"]
  R1 = Resistor [tolerance=±5% resistance=220 package="2010 [SMD]"]
  R2 = Resistor [tolerance=±5% resistance=220 package="2010 [SMD]"]
  R3 = Resistor [tolerance=±5% resistance=220 package="2010 [SMD]"]
  R4 = Resistor [tolerance=±5% resistance=220 package="2010 [SMD]"]
  R6 = Resistor [tolerance=±5% resistance=220 package="2010 [SMD]"]
  R7 = Resistor [tolerance=±5% resistance=220 package="2010 [SMD]"]
  R8 = Resistor [tolerance=±5% resistance=220 package="2010 [SMD]"]
  R5 = Resistor [tolerance=±5% resistance=220 package="0402 [SMD]"]
  R9 = Resistor [tolerance=±5% power=0.25W resistance=220 package=THT]
  R12 = Resistor [tolerance=±5% resistance=220 package="0805 [SMD]"]
  S1 = Pushbutton [package="[THT]"]
  S2 = Pushbutton [package="[THT]"]
  S3 = Pushbutton [package="[THT]"]
  S4 = Pushbutton [package="[THT]"]
  R13 = Resistor [tolerance=±5% resistance=220 package="0805 [SMD]"]
  R14 = Resistor [tolerance=±5% power=0.25W resistance=220 package=THT]

nets:
  N1: Part1.D21/SCL, Part2.SCL
  N2: Part1.D20/SDA, Part2.SDA
  N3: Part1.D10_PWM, IC1.SCK
  N4: Part1.D9_PWM, IC1.RCK
  N5: Part1.D8_PWM, IC1.SER
  5V: Part1.5V, RHT1.Vcc, Part2.5V, IC1.SCL, IC1.VCC
  GND: Part1.GND, RHT1.GND_1, J1.pin1, Part2.GND, IC1.GND, IC1.G, Q1.E, Q2.E, Q3.E, Q4.E, S1.Pin_3, S1.Pin_4, S2.Pin_3, S2.Pin_4, S3.Pin_3, S3.Pin_4, S4.Pin_3, S4.Pin_4
  N6: Part1.D2_PWM, RHT1.Data-signal
  N7: Part1.D4_PWM, S1.Pin_1, S1.Pin_2
  N8: Part1.D5_PWM, S2.Pin_1, S2.Pin_2
  N9: Part1.D6_PWM, S4.Pin_1, S4.Pin_2
  N10: Part1.D7_PWM, S3.Pin_1, S3.Pin_2
  N11: Part1.D46, R1.Pin_1
  N12: Part1.D48, R4.Pin_1
  N13: Part1.D50, R2.Pin_1
  N14: Part1.D52, R3.Pin_1
  N15: IC1.QB, LED1.F, R5.Pin_0, R5.Pin_1
  N16: IC1.QC, LED1.B, R6.Pin_0, R6.Pin_1
  N17: IC1.QD, LED1.E, R7.Pin_0, R7.Pin_1
  N18: IC1.QE, LED1.D, R8.Pin_0, R8.Pin_1
  N19: IC1.QF, LED1.DP, R12.Pin_0, R12.Pin_1
  N20: IC1.QG, LED1.C, R14.Pin_0, R14.Pin_1
  N21: IC1.QH, LED1.G, R9.Pin_0, R9.Pin_1
  N22: IC1.QA, LED1.A, R13.Pin_0, R13.Pin_1
  N23: LED1.DIG1, Q1.C
  N24: LED1.DIG2, Q4.C
  N25: LED1.DIG3, Q3.C
  N26: LED1.DIG4, Q2.C
  N27: Q1.B, R3.Pin_0
  N28: Q2.B, R1.Pin_0
  N29: Q3.B, R4.Pin_0
  N30: Q4.B, R2.Pin_0
